// Logisim project alu.circ as structural Verilog: 1 circuit, main circuit main
module main (
  input  [31:0] X,
  input  [31:0] Y,
  input  [3:0] Switch,
  output Signed_Overflow,
  output Equal,
  output [31:0] Result
);

  wire decoder_1_out3, decoder_1_out6, decoder_1_out10, decoder_1_out11, decoder_1_out12, decoder_1_out13;
  wire [31:0] and_1_out, controlled_buffer_1_out, controlled_buffer_2_out, controlled_buffer_3_out,
       controlled_buffer_4_out, controlled_buffer_5_out, controlled_buffer_6_out, controlled_buffer_7_out,
       controlled_buffer_8_out, controlled_buffer_9_out, controlled_buffer_10_out, or_1_out, xor_1_out;

  Decoder #(.select(4), .disabled(0), .enable("false")) decoder_1 (
    .out3(decoder_1_out3), .out6(decoder_1_out6), .out10(decoder_1_out10), .out11(decoder_1_out11),
    .out12(decoder_1_out12), .out13(decoder_1_out13), .sel(Switch));  // open: out0, out1, out2, out4, out5, out7, out8, out9, out14, out15
  assign controlled_buffer_1_out = decoder_1_out3 ? Y : 32'bz;  // Controlled_Buffer controlled_buffer_1
  assign controlled_buffer_2_out = decoder_1_out3 ? X : 32'bz;  // Controlled_Buffer controlled_buffer_2
  Adder #(.width(32)) adder_1 (
    .a(controlled_buffer_1_out), .b(controlled_buffer_2_out), .out(Result), .cout(Signed_Overflow));  // open: cin
  assign controlled_buffer_3_out = decoder_1_out10 ? Y : 32'bz;  // Controlled_Buffer controlled_buffer_3
  assign controlled_buffer_4_out = decoder_1_out10 ? X : 32'bz;  // Controlled_Buffer controlled_buffer_4
  assign controlled_buffer_5_out = decoder_1_out11 ? Y : 32'bz;  // Controlled_Buffer controlled_buffer_5
  assign controlled_buffer_6_out = decoder_1_out11 ? X : 32'bz;  // Controlled_Buffer controlled_buffer_6
  assign controlled_buffer_7_out = decoder_1_out12 ? Y : 32'bz;  // Controlled_Buffer controlled_buffer_7
  assign controlled_buffer_8_out = decoder_1_out12 ? X : 32'bz;  // Controlled_Buffer controlled_buffer_8
  assign controlled_buffer_9_out = decoder_1_out6 ? Y : 32'bz;  // Controlled_Buffer controlled_buffer_9
  assign controlled_buffer_10_out = decoder_1_out6 ? X : 32'bz;  // Controlled_Buffer controlled_buffer_10
  assign and_1_out = controlled_buffer_3_out & controlled_buffer_4_out;  // AND_Gate and_1, 32 bits wide
  assign or_1_out = controlled_buffer_5_out | controlled_buffer_6_out;  // OR_Gate or_1, 32 bits wide
  assign xor_1_out = controlled_buffer_7_out ^ controlled_buffer_8_out;  // XOR_Gate xor_1, 32 bits wide
  Subtractor #(.width(32)) subtractor_1 (
    .a(controlled_buffer_9_out), .b(controlled_buffer_10_out), .out(Result), .bout(Signed_Overflow));  // open: bin

  // Other names for the same wires on the sheet: overflow = Signed_Overflow; S[3:0] = Switch

  // Notes on the sheet:
  //   INPUTS to your circuit
  //   ADD
  //   DON'T CHANGE THE LOCATIONS OF THE INPUTS AND OUTPUTS!
  //   AND
  //   OR
  //   XOR
  //   SUB
  //   OUTPUTS from your circuit
endmodule
